// Logisim project processeur.circ as structural Verilog: 11 circuits, main circuit main
module main (
  input  Reset,
  input  ResetRAM
);

  wire Clock, Clock_out, Cond, CTRL, Exec, Fetch, getcst_2_imm, Load, ramctrl_1_memload, ramctrl_1_memstore,
       Store, WriteReg;
  wire [2:0] GetOp;
  wire [15:0] Addr, alu_1_output, Arg1, Arg2, bit_extender_2_out, getcst_1_cst, getcst_2_cst, JMP_Address,
       MemIN, PC, R0, R1, R2, R3, R4, R5, R6, R7;
  wire [31:0] bit_extender_1_out, IR, MemOUT;

  Clock u_Clock (.out(Clock_out));
  Seq seq_1 (.ClockOrig(Clock_out), .reset(Reset), .Fetch(Fetch), .Exec(Exec), .Clock(Clock));
  LED led_1 (.in(Clock_out));
  RegPC regpc_1 (.JMP_Address(JMP_Address), .Cond(Cond), .CTRL(CTRL), .Clock(Exec), .Reset(Reset), .PC(PC));
  // Probe on PC
  GetAddr getaddr_1 (.PC(PC), .Addr(Addr), .Fetch(Fetch), .Load(Load), .Store(Store), .SRout(Arg1));
  // Probe on Addr
  LED led_2 (.in(Fetch));
  LED led_3 (.in(Exec));
  CheckCond checkcond_1 (.Ope(GetOp), .MemIn(MemIN), .Arg1(Arg1), .in_3(CTRL), .Cond(Cond));
  // Probe on MemIN
  assign bit_extender_1_out = {{16{MemIN[15]}}, MemIN};  // Bit_Extender bit_extender_1
  // Probe on PC
  // Probe on IR
  DecodeIR decodeir_1 (
    .CTRL(CTRL), .WriteReg(WriteReg), .IR(IR), .Load(Load), .GetOp(GetOp), .JMPAddress(JMP_Address),
    .Store(Store), .in_1(getcst_1_cst));
  GetCst getcst_1 (.IR(IR), .Cst(getcst_1_cst));  // open: Imm
  RamCtrl ramctrl_1 (
    .Store(Store), .Fetch(Fetch), .Exec(Exec), .Load(Load), .MemStore(ramctrl_1_memstore),
    .MemLoad(ramctrl_1_memload), .Clock(Clock));
  // Probe on MemOUT
  RAM #(.addrWidth(16), .dataWidth(32), .bus("separate")) ram_1 (
    .addr(Addr), .din(bit_extender_1_out), .data(MemOUT), .str(ramctrl_1_memstore), .clk(ramctrl_1_memstore),
    .ld(ramctrl_1_memload), .clr(ResetRAM));  // open: sel
  // Probe on R0
  // Probe on R3
  // Probe on R6
  Register #(.width(32), .trigger("falling")) RegIR (.D(MemOUT), .Q(IR), .clk(Fetch), .clr(Reset));  // open: en
  // Probe on R1
  // Probe on R4
  // Probe on R7
  Pile pile_1 (.AdLigneCall(PC), .CTRL(CTRL), .GetOp(GetOp), .Top(JMP_Address), .ResetRAM(Reset), .Fetch(Fetch));
  // Probe on IR
  // Probe on R2
  // Probe on R5
  Bit_Extender #(.in_width(32), .\type ("sign")) bit_extender_2 (.in(MemOUT), .out(bit_extender_2_out));
  // Probe on IR[25:23]
  // Probe on IR[22:20]
  // Probe on IR[19:17]
  // Probe on getcst_2_cst
  GetCst getcst_2 (.IR(IR), .Cst(getcst_2_cst), .Imm(getcst_2_imm));
  Registres registres_1 (
    .IN(alu_1_output), .WriteReg(WriteReg), .DR(IR[25:23]), .OUT_SR1(Arg1), .OUT_SR2(Arg2), .OUT_DR(MemIN),
    .R0(R0), .R1(R1), .R2(R2), .R3(R3), .R4(R4), .R5(R5), .R6(R6), .R7(R7), .Reset(Reset), .Clock(Exec),
    .SR1(IR[22:20]), .SR2(IR[19:17]), .LD(Load), .MemOUT(bit_extender_2_out));
  // Probe on Arg2
  // Probe on Arg1
  ALU alu_1 (.Imm(getcst_2_imm), .e2(GetOp), .Input1(Arg1), .Input2(Arg2), .Cst(getcst_2_cst), .Output(alu_1_output));
  // Probe on alu_1_output
  // Probe on R0
  // Probe on R1
  // Probe on R2
  // Probe on R3
  // Probe on R4
  // Probe on R5
  // Probe on R6
  // Probe on R7
  // Probe on alu_1_output

  // Notes on the sheet:
  //   RAM
endmodule

module ALU (
  input  [15:0] Input1,
  input  [15:0] Input2,
  input  [15:0] Cst,
  input  Imm,
  input  [2:0] e2,
  output [15:0] Output
);

  wire comparator_1_gt, comparator_2_gt, not_1_out, Op1, Op2, Op3, Op4, Op5, Op6, Op7, Op8;
  wire [15:0] adder_1_out, and_1_out, controlled_buffer_1_out, controlled_buffer_3_out,
       controlled_buffer_4_out, controlled_buffer_5_out, controlled_buffer_6_out, controlled_buffer_7_out,
       controlled_buffer_8_out, controlled_buffer_9_out, controlled_buffer_10_out, controlled_buffer_11_out,
       controlled_buffer_12_out, controlled_buffer_13_out, controlled_buffer_14_out,
       controlled_buffer_15_out, controlled_buffer_16_out, multiplexer_1_out, multiplexer_2_out,
       multiplier_1_out, or_1_out, shifter_1_out, shifter_2_out, subtractor_1_out, xor_1_out;

  Decoder #(.select(3)) decoder_1 (
    .out0(Op1), .out1(Op2), .out2(Op3), .out3(Op4), .out4(Op5), .out5(Op6), .out6(Op7), .out7(Op8), .sel(e2));  // open: en
  not not_1 (not_1_out, Imm);
  assign controlled_buffer_1_out = not_1_out ? Input2 : 16'bz;  // Controlled_Buffer controlled_buffer_1
  assign controlled_buffer_1_out = Imm ? Cst : 16'bz;  // Controlled_Buffer controlled_buffer_2
  assign controlled_buffer_3_out = Op1 ? Input1 : 16'bz;  // Controlled_Buffer controlled_buffer_3
  assign controlled_buffer_4_out = Op1 ? controlled_buffer_1_out : 16'bz;  // Controlled_Buffer controlled_buffer_4
  assign controlled_buffer_5_out = Op2 ? Input1 : 16'bz;  // Controlled_Buffer controlled_buffer_5
  assign controlled_buffer_6_out = Op2 ? controlled_buffer_1_out : 16'bz;  // Controlled_Buffer controlled_buffer_6
  assign controlled_buffer_7_out = Op3 ? Input1 : 16'bz;  // Controlled_Buffer controlled_buffer_7
  assign controlled_buffer_8_out = Op3 ? controlled_buffer_1_out : 16'bz;  // Controlled_Buffer controlled_buffer_8
  assign controlled_buffer_9_out = Op4 ? Input1 : 16'bz;  // Controlled_Buffer controlled_buffer_9
  assign controlled_buffer_10_out = Op4 ? controlled_buffer_1_out : 16'bz;  // Controlled_Buffer controlled_buffer_10
  assign controlled_buffer_11_out = Op5 ? Input1 : 16'bz;  // Controlled_Buffer controlled_buffer_11
  assign controlled_buffer_12_out = Op5 ? controlled_buffer_1_out : 16'bz;  // Controlled_Buffer controlled_buffer_12
  assign controlled_buffer_13_out = Op6 ? Input1 : 16'bz;  // Controlled_Buffer controlled_buffer_13
  assign controlled_buffer_14_out = Op7 ? Input1 : 16'bz;  // Controlled_Buffer controlled_buffer_14
  assign controlled_buffer_15_out = Op8 ? Input1 : 16'bz;  // Controlled_Buffer controlled_buffer_15
  assign controlled_buffer_16_out = Op8 ? controlled_buffer_1_out : 16'bz;  // Controlled_Buffer controlled_buffer_16
  Adder #(.width(16)) adder_1 (
    .a(controlled_buffer_3_out), .b(controlled_buffer_4_out), .out(adder_1_out));  // open: cin, cout
  Subtractor #(.width(16)) subtractor_1 (
    .a(controlled_buffer_5_out), .b(controlled_buffer_6_out), .out(subtractor_1_out));  // open: bin, bout
  assign and_1_out = controlled_buffer_7_out & controlled_buffer_8_out;  // AND_Gate and_1, 16 bits wide
  assign or_1_out = controlled_buffer_9_out | controlled_buffer_10_out;  // OR_Gate or_1, 16 bits wide
  assign xor_1_out = controlled_buffer_11_out ^ controlled_buffer_12_out;  // XOR_Gate xor_1, 16 bits wide
  Shifter #(.width(16)) shifter_1 (
    .in(controlled_buffer_13_out), .\dist (controlled_buffer_1_out[3:0]), .out(shifter_1_out));
  Shifter #(.width(16), .shift("lr")) shifter_2 (
    .in(controlled_buffer_14_out), .\dist (controlled_buffer_1_out[3:0]), .out(shifter_2_out));
  Multiplier #(.width(16)) multiplier_1 (
    .a(controlled_buffer_15_out), .b(controlled_buffer_16_out), .out(multiplier_1_out));  // open: cin, cout
  Multiplexer #(.width(16)) multiplexer_1 (
    .in0(shifter_1_out), .in1({16{1'b0}}), .out(multiplexer_1_out), .sel(comparator_1_gt));  // open: en
  Comparator #(.width(16)) comparator_1 (
    .a(controlled_buffer_1_out), .b(16'h10), .gt(comparator_1_gt));  // open: eq, lt
  Multiplexer #(.width(16)) multiplexer_2 (
    .in0(shifter_2_out), .in1({16{1'b0}}), .out(multiplexer_2_out), .sel(comparator_2_gt));  // open: en
  Comparator #(.width(16)) comparator_2 (
    .a(controlled_buffer_1_out), .b(16'h10), .gt(comparator_2_gt));  // open: eq, lt
  Multiplexer #(.select(3), .width(16)) multiplexer_3 (
    .in0(adder_1_out), .in1(subtractor_1_out), .in2(and_1_out), .in3(or_1_out), .in4(xor_1_out),
    .in5(multiplexer_1_out), .in6(multiplexer_2_out), .in7(multiplier_1_out), .out(Output), .sel(e2));  // open: en
endmodule

module DecodeIR (
  input  [15:0] in_1,
  input  [31:0] IR,
  output [15:0] JMPAddress,
  output [2:0] GetOp,
  output WriteReg,
  output Store,
  output Load,
  output CTRL
);

  wire and_1_out, and_2_out, and_3_out, decoder_1_out6, not_1_out, not_2_out, not_3_out, not_4_out, not_5_out;

  Decoder #(.select(3)) decoder_1 (
    .out6(decoder_1_out6), .sel(IR[29:27]));  // open: out0, out1, out2, out3, out4, out5, out7, en
  assign JMPAddress = and_1_out ? in_1 : 16'bz;  // Controlled_Buffer controlled_buffer_1
  and and_1 (and_1_out, not_1_out, CTRL);
  not not_1 (not_1_out, decoder_1_out6);
  not not_2 (not_2_out, IR[31]);
  and and_2 (and_2_out, not_2_out, not_3_out);
  not not_3 (not_3_out, IR[30]);
  not not_4 (not_4_out, IR[31]);
  and and_3 (and_3_out, not_4_out, IR[30]);
  and and_4 (CTRL, IR[30], IR[31]);
  or or_1 (WriteReg, and_2_out, Load);
  not not_5 (not_5_out, IR[27]);
  and and_5 (Store, IR[27], and_3_out);
  and and_6 (Load, not_5_out, and_3_out);

  assign GetOp = IR[29:27];

  // Other names for the same wires on the sheet: Const[15:0] = IR[15:0]; RC[2:0] = IR[19:17]; RB[2:0] = IR[22:20];
  //   RA[2:0] = IR[25:23]; Immediat = IR[26]; Operation[2:0] = IR[29:27]; Instruction[1:0] = IR[31:30]
endmodule

module GetAddr (
  input  [15:0] SRout,
  input  [15:0] PC,
  input  Load,
  input  Store,
  input  Fetch,
  output [15:0] Addr
);

  wire and_1_out, not_1_out, not_2_out, or_1_out;

  not not_1 (not_1_out, Load);
  not not_2 (not_2_out, Store);
  and and_1 (and_1_out, not_1_out, not_2_out);
  Multiplexer #(.width(16)) multiplexer_1 (.in0(SRout), .in1(PC), .out(Addr), .sel(or_1_out));  // open: en
  or or_1 (or_1_out, and_1_out, Fetch);
endmodule

module GetCst (
  input  [31:0] IR,
  output [15:0] Cst,
  output Imm
);


  assign Cst = IR[15:0];
  assign Imm = IR[26];
endmodule

module RamCtrl (
  input  Clock,
  input  Exec,
  input  Fetch,
  input  Load,
  input  Store,
  output MemLoad,
  output MemStore
);

  wire and_1_out;

  and and_1 (and_1_out, Exec, Load);
  and and_2 (MemStore, Exec, Clock, Store);
  or or_1 (MemLoad, Fetch, and_1_out);
endmodule

module Registres (
  input  [15:0] IN,
  input  [15:0] MemOUT,
  input  LD,
  input  [2:0] SR1,
  input  [2:0] DR,
  input  WriteReg,
  input  [2:0] SR2,
  input  Clock,
  input  Reset,
  output [15:0] R0,
  output [15:0] OUT_SR1,
  output [15:0] R1,
  output [15:0] R2,
  output [15:0] R3,
  output [15:0] R4,
  output [15:0] OUT_SR2,
  output [15:0] R5,
  output [15:0] R6,
  output [15:0] R7,
  output [15:0] OUT_DR
);

  wire decoder_1_out0, decoder_1_out1, decoder_1_out2, decoder_1_out3, decoder_1_out4, decoder_1_out5,
       decoder_1_out6, decoder_1_out7;
  wire [15:0] multiplexer_1_out;

  Multiplexer #(.width(16)) multiplexer_1 (.in0(IN), .in1(MemOUT), .out(multiplexer_1_out), .sel(LD));  // open: en
  Decoder #(.select(3), .disabled(0)) decoder_1 (
    .out0(decoder_1_out0), .out1(decoder_1_out1), .out2(decoder_1_out2), .out3(decoder_1_out3),
    .out4(decoder_1_out4), .out5(decoder_1_out5), .out6(decoder_1_out6), .out7(decoder_1_out7), .sel(DR),
    .en(WriteReg));
  Register #(.width(16), .trigger("falling")) u_R0 (
    .D(multiplexer_1_out), .en(decoder_1_out0), .Q(R0), .clk(Clock), .clr(Reset));
  Register #(.width(16), .trigger("falling")) u_R1 (
    .D(multiplexer_1_out), .en(decoder_1_out1), .Q(R1), .clk(Clock), .clr(Reset));
  Register #(.width(16), .trigger("falling")) u_R2 (
    .D(multiplexer_1_out), .en(decoder_1_out2), .Q(R2), .clk(Clock), .clr(Reset));
  Register #(.width(16), .trigger("falling")) u_R3 (
    .D(multiplexer_1_out), .en(decoder_1_out3), .Q(R3), .clk(Clock), .clr(Reset));
  Register #(.width(16), .trigger("falling")) u_R4 (
    .D(multiplexer_1_out), .en(decoder_1_out4), .Q(R4), .clk(Clock), .clr(Reset));
  Register #(.width(16), .trigger("falling")) u_R5 (
    .D(multiplexer_1_out), .en(decoder_1_out5), .Q(R5), .clk(Clock), .clr(Reset));
  Register #(.width(16), .trigger("falling")) u_R6 (
    .D(multiplexer_1_out), .en(decoder_1_out6), .Q(R6), .clk(Clock), .clr(Reset));
  Register #(.width(16), .trigger("falling")) u_R7 (
    .D(multiplexer_1_out), .en(decoder_1_out7), .Q(R7), .clk(Clock), .clr(Reset));
  Multiplexer #(.select(3), .width(16)) multiplexer_2 (
    .in0(R0), .in1(R1), .in2(R2), .in3(R3), .in4(R4), .in5(R5), .in6(R6), .in7(R7), .out(OUT_SR1), .sel(SR1));  // open: en
  Multiplexer #(.select(3), .width(16)) multiplexer_3 (
    .in0(R0), .in1(R1), .in2(R2), .in3(R3), .in4(R4), .in5(R5), .in6(R6), .in7(R7), .out(OUT_SR2), .sel(SR2));  // open: en
  Multiplexer #(.select(3), .width(16)) multiplexer_4 (
    .in0(R0), .in1(R1), .in2(R2), .in3(R3), .in4(R4), .in5(R5), .in6(R6), .in7(R7), .out(OUT_DR), .sel(DR));  // open: en
endmodule

module RegPC (
  input  [15:0] JMP_Address,
  input  Cond,
  input  CTRL,
  input  Clock,
  input  Reset,
  output [15:0] PC
);

  wire and_1_out;
  wire [15:0] adder_1_out, multiplexer_1_out;

  and and_1 (and_1_out, Cond, CTRL);
  Adder #(.width(16)) adder_1 (.a(PC), .b(16'h1), .out(adder_1_out));  // open: cin, cout
  Multiplexer #(.width(16)) multiplexer_1 (
    .in0(adder_1_out), .in1(JMP_Address), .out(multiplexer_1_out), .sel(and_1_out));  // open: en
  Register #(.width(16), .trigger("falling")) u_PC (
    .D(multiplexer_1_out), .Q(PC), .clk(Clock), .clr(Reset));  // open: en
endmodule

module Seq (
  input  ClockOrig,
  input  reset,
  output Fetch,
  output Exec,
  output Clock
);

  Register #(.width(1), .trigger("falling")) register_1 (
    .D(Fetch), .Q(Exec), .clk(ClockOrig), .clr(reset));  // open: en
  not not_1 (Fetch, Exec);
  buf buffer_1 (Clock, ClockOrig);
endmodule

module CheckCond (
  input  [15:0] MemIn,
  input  [15:0] Arg1,
  input  in_3,
  input  [2:0] Ope,
  output Cond
);

  wire and_1_out, and_2_out, and_3_out, and_4_out, comparator_1_eq, comparator_2_eq, comparator_3_gt,
       comparator_4_lt, decoder_1_out0, decoder_1_out1, decoder_1_out2, decoder_1_out3, decoder_1_out4,
       decoder_1_out5, decoder_1_out6, not_1_out, or_1_out;

  Decoder #(.select(3), .enable("false")) decoder_1 (
    .out0(decoder_1_out0), .out1(decoder_1_out1), .out2(decoder_1_out2), .out3(decoder_1_out3),
    .out4(decoder_1_out4), .out5(decoder_1_out5), .out6(decoder_1_out6), .sel(Ope));  // open: out7
  Comparator #(.width(16)) comparator_1 (.a(MemIn), .b(Arg1), .eq(comparator_1_eq));  // open: gt, lt
  not not_1 (not_1_out, comparator_2_eq);
  Comparator #(.width(16)) comparator_2 (.a(MemIn), .b(Arg1), .eq(comparator_2_eq));  // open: gt, lt
  Comparator #(.width(16)) comparator_3 (.a(MemIn), .b(Arg1), .gt(comparator_3_gt));  // open: eq, lt
  Comparator #(.width(16)) comparator_4 (.a(MemIn), .b(Arg1), .lt(comparator_4_lt));  // open: gt, eq
  and and_1 (and_1_out, decoder_1_out0, comparator_1_eq);
  and and_2 (and_2_out, decoder_1_out1, not_1_out);
  and and_3 (and_3_out, decoder_1_out2, comparator_3_gt);
  and and_4 (and_4_out, decoder_1_out3, comparator_4_lt);
  or or_1 (or_1_out, and_1_out, and_2_out, and_3_out, and_4_out, decoder_1_out4, decoder_1_out5, decoder_1_out6);
  and and_5 (Cond, or_1_out, in_3);
endmodule

module Pile (
  input  ResetRAM,
  input  [15:0] AdLigneCall,
  input  CTRL,
  input  [2:0] GetOp,
  input  Fetch,
  output [15:0] Top
);

  wire and_1_out, and_2_out, and_3_out, decoder_1_out5, decoder_1_out6, or_1_out;
  wire [15:0] adder_1_out, adder_2_out, multiplexer_1_out, multiplexer_2_out, SP_q, subtractor_1_out,
       subtractor_2_out;

  Decoder #(.select(3)) decoder_1 (
    .out5(decoder_1_out5), .out6(decoder_1_out6), .sel(GetOp));  // open: out0, out1, out2, out3, out4, out7, en
  Subtractor #(.width(16)) subtractor_1 (.a(SP_q), .b(16'h1), .out(subtractor_1_out));  // open: bin, bout
  Adder #(.width(16)) adder_1 (.a(AdLigneCall), .b(16'h1), .out(adder_1_out));  // open: cin, cout
  and and_1 (and_1_out, decoder_1_out5, CTRL);
  and and_2 (and_2_out, CTRL, decoder_1_out6);
  Multiplexer #(.width(16)) multiplexer_1 (
    .in0(SP_q), .in1(subtractor_1_out), .out(multiplexer_1_out), .sel(and_2_out));  // open: en
  RAM #(.addrWidth(16), .dataWidth(16), .bus("separate")) ram_1 (
    .addr(multiplexer_1_out), .din(adder_1_out), .data(Top), .str(and_1_out), .clk(and_3_out),
    .ld(and_2_out), .clr(ResetRAM));  // open: sel
  Subtractor #(.width(16)) subtractor_2 (.a(SP_q), .b(16'h1), .out(subtractor_2_out));  // open: bin, bout
  Adder #(.width(16)) adder_2 (.a(SP_q), .b(16'h1), .out(adder_2_out));  // open: cin, cout
  or or_1 (or_1_out, and_1_out, and_2_out);
  Multiplexer #(.width(16)) multiplexer_2 (
    .in0(subtractor_2_out), .in1(adder_2_out), .out(multiplexer_2_out), .sel(and_1_out), .en(or_1_out));
  and and_3 (and_3_out, or_1_out, Fetch);
  Register #(.width(16), .trigger("falling")) SP (
    .D(multiplexer_2_out), .Q(SP_q), .clk(and_3_out), .clr(ResetRAM));  // open: en

  // Other names for the same wires on the sheet: Reset = ResetRAM
endmodule
